# Fritzing sketch Gráfico de montaje (saved by Fritzing 0.9.3b)

parts:
  Componente1 = Arduino Uno (Rev3)
  IC1 = Voltage Regulator [package=to-220-alt]
  GY1 = GY-521 (MPU-6050) [form="♀ (female)" package=THT]
  BAT1 = LIPO-1000mAh [package=lipo-1000]
  hc-sr1 = hc-sr04
  J10 = Basic Servo
  JP7 = Header 10 [package=1x10-2mm-smd]
  JP8 = Header 10 [package=1x10-2mm-smd]
  S1 = Toggle Switch [package=THT]
  J7 = Basic Servo
  J11 = Basic Servo
  J12 = Basic Servo
  J6 = Basic Servo
  J13 = Basic Servo
  J8 = Basic Servo
  J2 = Basic Servo
  LED1 = RGB LED - (4 legs) [package="5 mm [THT]"]
  R1 = Resistor [tolerance=±5% resistance=220 package="2010 [SMD]"]
  R2 = Resistor [tolerance=±5% resistance=220 package="2010 [SMD]"]

nets:
  N1: Componente1.A4/SDA, GY1.pin4
  N2: Componente1.A5/SCL, GY1.pin3
  N3: Componente1.D8, J2.pulse
  N4: Componente1.D9_PWM, J11.pulse
  N5: Componente1.D10_PWM/SS, J12.pulse
  N6: Componente1.D11_PWM/MOSI, J13.pulse
  N7: Componente1.D12/MISO, R1.Pin_1
  N8: Componente1.D13/SCK, R2.Pin_1
  N9: Componente1.GND, GY1.pin2, LED1.red_cathode
  N10: Componente1.D2, hc-sr1.Trig
  N11: Componente1.D3_PWM, hc-sr1.Echo
  N12: Componente1.D4, J8.pulse
  N13: Componente1.D5_PWM, J6.pulse
  N14: Componente1.D6_PWM, J7.pulse
  N15: Componente1.D7, J10.pulse
  N16: Componente1.3V3, GY1.pin1
  5V: Componente1.5V, hc-sr1.VCC
  VIN: Componente1.VIN, IC1.GND, S1.L2
  N17: IC1.OUT, JP8.1
  N18: BAT1.+, S1.COM
  N19: BAT1.-, JP7.1
  N20: J10.gnd, JP7.7
  N21: J10.vcc, JP8.7
  N22: JP7.2, J13.gnd
  N23: JP7.3, J12.gnd
  N24: JP7.4, J11.gnd
  N25: JP7.5, J2.gnd
  N26: JP7.8, J7.gnd
  N27: JP7.9, J6.gnd
  N28: JP7.10, J8.gnd
  N29: JP8.2, J13.vcc
  N30: JP8.3, J12.vcc
  N31: JP8.4, J11.vcc
  N32: JP8.5, J2.vcc
  N33: JP8.8, J7.vcc
  N34: JP8.9, J6.vcc
  N35: JP8.10, J8.vcc

custom parts:
  GY-521 (MPU-6050): Placa GY-521 basada en conjunto de acelerómetro+giroscopios MPU-6050
