# Fritzing sketch Plano electrico alimentacion servos (saved by Fritzing 0.9.3b)

parts:
  Zócalos_de_fase = Header 8 [package=1x08_smd_alt]
  Conectores_macho = Header 2 [package=jst-2-pth]
  Zócalos_GND = Header 8 [package=1x08_smd_alt]
  IC1 = Voltage Regulator [package=to220-igo]
  LM7805 = Voltage Regulator [package=78xxl]

nets:
  N1: Zócalos_de_fase.1, Zócalos_de_fase.2, Zócalos_de_fase.3, Zócalos_de_fase.4, Zócalos_de_fase.5, Zócalos_de_fase.6, Zócalos_de_fase.7, Zócalos_de_fase.8, IC1.OUT, LM7805.OUT
  GND: Conectores_macho.1, Zócalos_GND.1, Zócalos_GND.2, Zócalos_GND.3, Zócalos_GND.4, Zócalos_GND.5, Zócalos_GND.6, Zócalos_GND.7, Zócalos_GND.8, IC1.GND, LM7805.GND
  N2: Conectores_macho.2, IC1.IN, LM7805.IN
