# Fritzing sketch Plano electrico global (saved by Fritzing 0.9.3b)

parts:
  Regulador_de_tensión_7805 = Voltage Regulator [package=to-220-alt]
  GY-521 = GY-521 (MPU-6050) [form="♀ (female)" package=THT]
  7_4V_1000mAh = LIPO-1000mAh [package=lipo-1000]
  J10 = Basic Servo
  Zócalos_(tierra) = Header 10 [package=1x10-2mm-smd]
  Interruptor = Toggle Switch [package=THT]
  J7 = Basic Servo
  J11 = Basic Servo
  J12 = Basic Servo
  J6 = Basic Servo
  J13 = Basic Servo
  J8 = Basic Servo
  J2 = Basic Servo
  LED1 = RGB LED - (4 legs) [package="5 mm [THT]"]
  R1 = Resistor [tolerance=±5% resistance=220 package="2010 [SMD]"]
  R2 = Resistor [tolerance=±5% resistance=220 package="2010 [SMD]"]
  Zócalos_(fase) = Header 10 [package=1x10-2mm-smd]
  Componente1 = Arduino Uno (Rev3)
  hc-sr2 = hc-sr04

nets:
  GND: Regulador_de_tensión_7805.GND, GY-521.pin2, 7_4V_1000mAh.-, J10.gnd, Zócalos_(tierra).1, Zócalos_(tierra).2, Zócalos_(tierra).3, Zócalos_(tierra).4, Zócalos_(tierra).5, Zócalos_(tierra).6, Zócalos_(tierra).7, Zócalos_(tierra).8, Zócalos_(tierra).9, Zócalos_(tierra).10, J7.gnd, J11.gnd, J12.gnd, J6.gnd, J13.gnd, J8.gnd, J2.gnd, LED1.red_cathode, R1.Pin_0, R1.Pin_1, R2.Pin_0, Componente1.GND, hc-sr2.GND
  N1: Regulador_de_tensión_7805.IN, Interruptor.L1, Componente1.VIN
  VCC: Regulador_de_tensión_7805.OUT, J10.vcc, J7.vcc, J11.vcc, J12.vcc, J6.vcc, J13.vcc, J8.vcc, J2.vcc, Zócalos_(fase).1, Zócalos_(fase).2, Zócalos_(fase).3, Zócalos_(fase).4, Zócalos_(fase).5, Zócalos_(fase).6, Zócalos_(fase).7, Zócalos_(fase).8, Zócalos_(fase).9, Zócalos_(fase).10
  N2: GY-521.pin1, Componente1.3V3
  N3: GY-521.pin3, Componente1.A5/SCL
  N4: GY-521.pin4, Componente1.A4/SDA
  N5: 7_4V_1000mAh.+, Interruptor.COM
  N6: J10.pulse, Componente1.D7
  N7: J7.pulse, Componente1.D6_PWM
  N8: J11.pulse, Componente1.D5_PWM
  N9: J12.pulse, Componente1.D11_PWM/MOSI
  N10: J6.pulse, Componente1.D8
  N11: J13.pulse, Componente1.D9_PWM
  N12: J8.pulse, Componente1.D10_PWM/SS
  N13: J2.pulse, Componente1.D4
  N14: LED1.common_anode, Componente1.D12/MISO, Componente1.D13/SCK
  N15: LED1.green_cathode, R2.Pin_1
  N16: Componente1.D2, hc-sr2.Trig
  N17: Componente1.D3_PWM, hc-sr2.Echo
  5V: Componente1.5V, hc-sr2.VCC

custom parts:
  GY-521 (MPU-6050): Placa GY-521 basada en conjunto de acelerómetro+giroscopios MPU-6050
  hc-sr04: This is a HC-SR04 Distance Sensor
